// Digital circuit state-machine-110.dig as structural Verilog
module state_machine_110 (
  input  CLK,
  input  Input_X,
  output Output_x
);

  wire and_1_out, and_2_out, not_1_out, or_1_out, S_0_nq, S_0_q, S_1_nq, S_1_q;

  D_FF S_1 (.D(or_1_out), .C(CLK), .Q(S_1_q), .nQ(S_1_nq));
  not not_1 (not_1_out, Input_X);
  and and_1 (and_1_out, S_1_q, not_1_out);
  D_FF S_0 (.D(Input_X), .C(CLK), .Q(S_0_q), .nQ(S_0_nq));
  and and_2 (and_2_out, Input_X, S_0_q);
  and and_3 (Output_x, S_0_nq, S_1_nq);
  or or_1 (or_1_out, and_1_out, and_2_out);
endmodule
