// Digital circuit two-bit-up-down.dig as structural Verilog
module two_bit_up_down (
  input  CLK,
  input  Input
);

  wire FF0_nq, FF0_q, FF1_q, not_1_out, xor_1_out, xor_2_out;

  D_FF FF0 (.D(not_1_out), .C(CLK), .Q(FF0_q), .nQ(FF0_nq));
  not not_1 (not_1_out, FF0_q);
  xor xor_1 (xor_1_out, Input, FF0_nq);
  D_FF FF1 (.D(xor_2_out), .C(CLK), .Q(FF1_q));  // open: nQ
  xor xor_2 (xor_2_out, xor_1_out, FF1_q);
endmodule
